# Fritzing sketch dali_clock (saved by Fritzing 0.9.3b)

parts:
  Arduino = Arduino Uno (Rev3) - ICSP
  RTC = DS1302 [package="SO8 [SMD]"]
  FT810 = Header 5x2 [package=2x5-ra]

nets:
  N1: Arduino.ICSP_MOSI, Arduino.D11_PWM/MOSI, FT810.MOSI
  5V: Arduino.5V, RTC.VCC, FT810.5V
  GND: Arduino.GND, RTC.GND, FT810.GND
  N2: Arduino.D8, RTC.CLK
  N3: Arduino.D9_PWM, FT810.PD
  N4: Arduino.D10_PWM/SS, FT810.CS
  N5: Arduino.D12/MISO, FT810.MISO
  N6: Arduino.D13/SCK, FT810.SCK
  N7: Arduino.D6_PWM, RTC.RST
  N8: Arduino.D7, RTC.DAT

custom parts:
  DS1302: DS1302 SPI Real Time Clock
  Header 5x2: Header 5x2 Standard 10-pin dual row 0.1 header. Commonly used with AVR-ISP. Use with Spark Fun Electronics SKU: PRT-00778
